# Fritzing sketch CardDealer (saved by Fritzing 0.9.10b)
breadboards: 1

parts:
  Arduino_Uno = Arduino Uno (Rev3) - ICSP
  ServoDealer = Tower Pro SG90 servo [part_number=101246]
  ServoRotor = Tower Pro SG90 servo [part_number=101246]
  7_Segment = 7 Segment Display
  Resistor_220_Ohm = Resistor [tolerance=±5% power=0.25 resistance=220 package=THT]
  JoyStick = Thumb Joystick
  Resistor_10K_Ohm = Resistor [tolerance=±5% resistance=10k package="1206 [SMD]"]
  Button_Next = Pushbutton [package="[THT]"]
  Button_OK = Pushbutton [package="[THT]"]
  Resistor_10K_Ohm_2 = Resistor [tolerance=±5% resistance=10k package="1206 [SMD]"]
  Arduino_Mega = Arduino Mega 2560 (Rev3)

nets:
  N1: Arduino_Uno.A3, JoyStick.VERT
  N2: Arduino_Uno.D8, 7_Segment.Segment_G
  N3: Arduino_Uno.D9_PWM, ServoRotor.Signal
  N4: Arduino_Uno.D10_PWM/SS, ServoDealer.Signal
  N5: Arduino_Uno.D11_PWM/MOSI, 7_Segment.Segment_E
  N6: Arduino_Uno.D12/MISO, 7_Segment.Segment_F
  N7: Arduino_Uno.D13/SCK, 7_Segment.Segment_A
  N8: Arduino_Uno.D3_PWM, Button_OK.Pin_1, Button_OK.Pin_2, Resistor_10K_Ohm_2.Pin_1
  N9: Arduino_Uno.D5_PWM, 7_Segment.Segment_D
  N10: Arduino_Uno.D6_PWM, 7_Segment.common_anode#12
  N11: Arduino_Uno.D7, 7_Segment.Segment_B
  N12: Arduino_Uno.5V, Resistor_220_Ohm.Pin_0, Button_Next.Pin_3, Button_Next.Pin_4, Button_OK.Pin_3, Button_OK.Pin_4
  N13: Arduino_Uno.GND, Resistor_10K_Ohm.Pin_0, Resistor_10K_Ohm_2.Pin_0
  +5V: ServoDealer.+5V, Arduino_Mega.5V
  GND: ServoDealer.GND, ServoRotor.GND, Arduino_Mega.GND
  N14: 7_Segment.common_anode#5, 7_Segment.common_anode#16, Resistor_220_Ohm.Pin_1
  N15: Resistor_10K_Ohm.Pin_1, Button_Next.Pin_1, Button_Next.Pin_2

custom parts:
  Tower Pro SG90 servo: Original file by John De Cristofaro http://www.adafruit.com/products/1449 Adafruit Feedback Servo (Small) Edited by: e-radionica.com 28/9/2015
